# Fritzing sketch Blackpill MPU6050 wiring (saved by Fritzing 0.9.3b)

parts:
  A1 = weact studio black pill
  GY1 = MPU-6050 Board GY-521 [form="♀ (female)" package=THT]
  LED1 = LED - 5mm [color="Red (633nm)" package="5 mm [THT]"]

nets:
  N1: A1.Pin_6, LED1.anode
  N2: A1.Pin_23, GY1.pin2
  N3: A1.Pin_24, GY1.pin1
  N4: A1.Pin_38, GY1.pin3
  N5: A1.Pin_39, GY1.pin4

custom parts:
  weact studio black pill: The STM32F401CE based Black Pill V3.0+ Board.
  MPU-6050 Board GY-521: Acelerometro y Giroscopio MPU-6050 Board GY-521
